// Logisim project hi.circ as structural Verilog
module Warmup (
  input  in_1
);

  wire clock_1_out, d_ff_1_q;

  Clock #(.highDuration(3), .lowDuration(3), .phaseOffset(1)) clock_1 (.out(clock_1_out));
  D_Flip_Flop #(.trigger("high")) d_ff_1 (.D(in_1), .clk(clock_1_out), .Q(d_ff_1_q));  // open: Qn, preset, reset
  LED led_1 (.in(d_ff_1_q));
endmodule

module FA (
  input  B,
  input  A,
  input  Cin,
  output S,
  output Cout
);

  wire and_1_out, and_2_out, xor_1_out;

  xor xor_1 (xor_1_out, A, B);
  and and_1 (and_1_out, A, B);
  xor xor_2 (S, xor_1_out, Cin);
  and and_2 (and_2_out, Cin, xor_1_out);
  or or_1 (Cout, and_1_out, and_2_out);
endmodule

module ADDSUB4 (
  input  Sub,
  input  [3:0] B,
  input  [3:0] A,
  output [3:0] S,
  output C3,
  output C2,
  output C1,
  output Z,
  output N,
  output C,
  output V
);

  wire xor_1_out, xor_2_out, xor_3_out, xor_4_out, xor_5_out, xor_6_out;

  xor xor_1 (xor_1_out, Sub, B[0]);
  xor xor_2 (xor_2_out, Sub, B[1]);
  xor xor_3 (xor_3_out, Sub, B[2]);
  xor xor_4 (xor_4_out, Sub, B[3]);
  FA fa_1 (.B(xor_1_out), .A(A[0]), .Cin(Sub), .S(S[0]), .Cout(C1));
  FA fa_2 (.B(xor_2_out), .A(A[1]), .Cin(C1), .S(S[1]), .Cout(C2));
  FA fa_3 (.B(xor_3_out), .A(A[2]), .Cin(C2), .S(S[2]), .Cout(C3));
  xor xor_5 (xor_5_out, N, xor_4_out);
  and and_1 (V, xor_5_out, xor_6_out);
  xor xor_6 (xor_6_out, N, A[3]);
  FA fa_4 (.B(xor_4_out), .A(A[3]), .Cin(C3), .S(N), .Cout(C));
  nor nor_1 (Z, S[0], S[1], S[2], N);

  assign S[3] = N;
endmodule

module ALU8 (
  input  [7:0] A,
  input  [2:0] OP,
  input  [7:0] B,
  input  [7:0] in_4,
  input  [7:0] in_5,
  output [7:0] R,
  output Z,
  output LT
);

  wire [7:0] adder_1_out, adder_2_out, and_1_out, multiplexer_1_out, multiplexer_2_out, not_1_out, or_1_out,
       subtractor_1_out, subtractor_2_out, xor_1_out;

  assign not_1_out = ~A;  // NOT_Gate not_1, 8 bits wide
  Adder adder_1 (.a(A), .b(B), .out(adder_1_out));  // open: cin, cout
  Adder adder_2 (.a(A), .b(in_4), .out(adder_2_out));  // open: cin, cout
  Subtractor subtractor_1 (.a(A), .b(B), .out(subtractor_1_out));  // open: bin, bout
  Subtractor subtractor_2 (.a(A), .b(in_5), .out(subtractor_2_out));  // open: bin, bout
  assign and_1_out = A & B;  // AND_Gate and_1, 8 bits wide
  assign or_1_out = A | B;  // OR_Gate or_1, 8 bits wide
  assign xor_1_out = A ^ B;  // XOR_Gate xor_1, 8 bits wide
  Multiplexer #(.select(2), .width(8)) multiplexer_1 (
    .in0(adder_1_out), .in1(adder_2_out), .in2(subtractor_1_out), .in3(subtractor_2_out),
    .out(multiplexer_1_out), .sel(OP[1:0]));
  Multiplexer #(.select(2), .width(8)) multiplexer_2 (
    .in0(and_1_out), .in1(or_1_out), .in2(not_1_out), .in3(xor_1_out), .out(multiplexer_2_out), .sel(OP[1:0]));
  Multiplexer #(.width(8)) multiplexer_3 (.in0(multiplexer_1_out), .in1(multiplexer_2_out), .out(R), .sel(OP[2]));
  nor nor_1 (Z, R[7], R[6], R[5], R[4], R[3], R[2], R[1], R[0]);
  con con_1 (.A7(A[7]), .B7(B[7]), .R7(R[7]), .LT(LT));
endmodule

module con (
  input  A7,
  input  B7,
  input  R7,
  output LT
);

  wire and_1_out, and_2_out, not_1_out, not_2_out, xor_1_out;

  not not_1 (not_1_out, B7);
  xor xor_1 (xor_1_out, A7, B7);
  and and_1 (and_1_out, A7, not_1_out);
  not not_2 (not_2_out, xor_1_out);
  and and_2 (and_2_out, not_2_out, R7);
  or or_1 (LT, and_1_out, and_2_out);
endmodule
